// Logisim project kodelaas_larshalv.circ as structural Verilog: 2 circuits, main circuit main
module main (
);

  wire _0_2_q, _1_2_q, _1_out, _2_out, _3_out, _4_out, _5_out, _6_out, _7_out, Clock_out, kodelogikk_1_d0,
       kodelogikk_1_d1, kodelogikk_1_out;
  wire [2:0] priority_encoder_1_out;

  Button _1 (.out(_1_out));
  Button _4 (.out(_4_out));
  Button _7 (.out(_7_out));
  Button button ();  // open: out
  Button _2 (.out(_2_out));
  Button _5 (.out(_5_out));
  Button _8 ();  // open: out
  Button button_2 ();  // open: out
  Button _0 ();  // open: out
  Button _3 (.out(_3_out));
  Button _6 (.out(_6_out));
  Button _9 ();  // open: out
  Priority_Encoder #(.disabled(0)) priority_encoder_1 (
    .in1(_1_out), .in2(_2_out), .in3(_3_out), .in4(_4_out), .in5(_5_out), .in6(_6_out), .in7(_7_out),
    .out(priority_encoder_1_out));  // open: in0, en_in, gs, en_out
  Clock Clock (.out(Clock_out));
  Kodelogikk kodelogikk_1 (
    .Q1(_1_2_q), .Q0(_0_2_q), .x2(priority_encoder_1_out[2]), .D1(kodelogikk_1_d1),
    .x1(priority_encoder_1_out[1]), .x0(priority_encoder_1_out[0]), .D0(kodelogikk_1_d0),
    .Out(kodelogikk_1_out));
  D_Flip_Flop _1_2 (.clk(Clock_out), .D(kodelogikk_1_d1), .Q(_1_2_q));  // open: Qn, preset, en, reset
  D_Flip_Flop _0_2 (.clk(Clock_out), .D(kodelogikk_1_d0), .Q(_0_2_q));  // open: Qn, preset, en, reset
  LED Out (.in(kodelogikk_1_out));

  // Notes on the sheet:
  //   Kode: 7-2-5
endmodule

module Kodelogikk (
  input  Q1,
  input  Q0,
  input  x2,
  input  x1,
  input  x0,
  output D1,
  output D0,
  output Out
);

  wire and_2_out, and_3_out, and_4_out, and_5_out, and_6_out, and_7_out, not_1_out, not_2_out, not_3_out,
       not_4_out, not_5_out, not_6_out, not_7_out, not_8_out, not_9_out, not_10_out, not_11_out, not_12_out,
       not_13_out, not_14_out;

  not not_1 (not_1_out, Q1);
  not not_2 (not_2_out, x2);
  not not_3 (not_3_out, x0);
  not not_4 (not_4_out, Q0);
  not not_5 (not_5_out, x2);
  not not_6 (not_6_out, x0);
  not not_7 (not_7_out, Q0);
  not not_8 (not_8_out, x1);
  not not_9 (not_9_out, Q1);
  not not_10 (not_10_out, Q1);
  not not_11 (not_11_out, x2);
  not not_12 (not_12_out, x1);
  not not_13 (not_13_out, x0);
  not not_14 (not_14_out, Q0);
  and and_1 (Out, Q1, Q0);
  and and_2 (and_2_out, not_1_out, Q0, not_2_out, x1, not_3_out);
  and and_3 (and_3_out, Q1, not_4_out, not_5_out, not_6_out);
  and and_4 (and_4_out, Q1, not_7_out, x2, not_8_out, x0);
  and and_5 (and_5_out, not_9_out, x2, x1, x0);
  and and_6 (and_6_out, not_10_out, Q0, not_11_out, not_12_out, not_13_out);
  and and_7 (and_7_out, Q1, not_14_out, x2, x0);
  or or_1 (D1, and_2_out, and_3_out, and_4_out);
  or or_2 (D0, and_5_out, and_6_out, and_7_out);
endmodule
