// Logisim project larshalv_oblig1.circ as structural Verilog: 3 circuits, main circuit main
module main (
  input  A3,
  input  A2,
  input  A1,
  input  A0,
  input  Fortegn,
  output Overflow,
  output V,
  output S7,
  output S6,
  output S5,
  output S4,
  output S3,
  output S2,
  output S1,
  output S0
);

  wire full_adder_2_c_1, full_adder_2_s, full_adder_3_c_1, full_adder_3_s, full_adder_4_c_1,
       full_adder_5_c_1, full_adder_6_c_1, full_adder_6_s, full_adder_7_c_1, full_adder_8_c_1,
       full_adder_8_s, full_adder_9_c_1, full_adder_9_s, full_adder_10_c_1, full_adder_11_c_1,
       full_adder_12_c_1, full_adder_12_s, full_adder_13_c_1, full_adder_14_c_1, halv_adder_1_c,
       halv_adder_1_s, nand_1_out, not_1_out, not_2_out, not_3_out, not_4_out, xor_1_out, xor_2_out,
       xor_3_out, xor_4_out, xor_5_out, xor_6_out, xor_7_out, xor_8_out;

  not not_1 (not_1_out, A1);
  not not_2 (not_2_out, A2);
  not not_3 (not_3_out, A3);
  nand nand_1 (nand_1_out, not_3_out, not_2_out, not_1_out, not_4_out);
  and and_1 (V, nand_1_out, Fortegn);
  not not_4 (not_4_out, A0);
  xor xor_1 (xor_1_out, full_adder_3_c_1, Fortegn);
  Full_adder full_adder_1 (.C_1(Overflow), .A(1'b0), .B(xor_1_out), .S(S7), .C(full_adder_5_c_1));
  Full_adder full_adder_2 (.C_1(full_adder_2_c_1), .A(A2), .B(1'b0), .S(full_adder_2_s), .C(full_adder_6_c_1));
  Full_adder full_adder_3 (.C_1(full_adder_3_c_1), .A(A3), .B(1'b0), .S(full_adder_3_s), .C(full_adder_2_c_1));
  xor xor_2 (xor_2_out, full_adder_3_s, Fortegn);
  xor xor_3 (xor_3_out, full_adder_2_s, Fortegn);
  Full_adder full_adder_4 (.C_1(full_adder_4_c_1), .A(1'b0), .B(xor_3_out), .S(S5), .C(full_adder_7_c_1));
  Full_adder full_adder_5 (.C_1(full_adder_5_c_1), .A(1'b0), .B(xor_2_out), .S(S6), .C(full_adder_4_c_1));
  Full_adder full_adder_6 (.C_1(full_adder_6_c_1), .A(A1), .B(A3), .S(full_adder_6_s), .C(full_adder_9_c_1));
  xor xor_4 (xor_4_out, full_adder_6_s, Fortegn);
  Full_adder full_adder_7 (.C_1(full_adder_7_c_1), .A(1'b0), .B(xor_4_out), .S(S4), .C(full_adder_10_c_1));
  Full_adder full_adder_8 (.C_1(full_adder_8_c_1), .A(1'b0), .B(A1), .S(full_adder_8_s), .C(full_adder_12_c_1));
  Full_adder full_adder_9 (.C_1(full_adder_9_c_1), .A(A0), .B(A2), .S(full_adder_9_s), .C(full_adder_8_c_1));
  xor xor_5 (xor_5_out, full_adder_9_s, Fortegn);
  xor xor_6 (xor_6_out, full_adder_8_s, Fortegn);
  Full_adder full_adder_10 (.C_1(full_adder_10_c_1), .A(1'b0), .B(xor_5_out), .S(S3), .C(full_adder_11_c_1));
  Full_adder full_adder_11 (.C_1(full_adder_11_c_1), .A(1'b0), .B(xor_6_out), .S(S2), .C(full_adder_13_c_1));
  Full_adder full_adder_12 (.C_1(full_adder_12_c_1), .A(1'b0), .B(A0), .S(full_adder_12_s), .C(halv_adder_1_c));
  xor xor_7 (xor_7_out, halv_adder_1_s, Fortegn);
  xor xor_8 (xor_8_out, full_adder_12_s, Fortegn);
  Full_adder full_adder_13 (.C_1(full_adder_13_c_1), .A(1'b0), .B(xor_8_out), .S(S1), .C(full_adder_14_c_1));
  Halv_adder halv_adder_1 (.A(1'b0), .B(1'b0), .S(halv_adder_1_s), .C(halv_adder_1_c));
  Full_adder full_adder_14 (.C_1(full_adder_14_c_1), .A(1'b0), .B(xor_7_out), .S(S0), .C(Fortegn));

  // Notes on the sheet:
  //   0 = (+)10
  //   1 = (-)10
endmodule

// Halv
module Halv_adder (
  input  A,
  input  B,
  output S,
  output C
);

  xor xor_1 (S, A, B);
  and and_1 (C, A, B);
endmodule

// Full
module Full_adder (
  input  A,
  input  B,
  input  C,
  output S,
  output C_1
);

  wire and_1_out, and_2_out, xor_1_out;

  xor xor_1 (xor_1_out, A, B);
  and and_1 (and_1_out, A, B);
  xor xor_2 (S, xor_1_out, C);
  and and_2 (and_2_out, xor_1_out, C);
  or or_1 (C_1, and_2_out, and_1_out);
endmodule
