// Logisim project Oblig_2.circ as structural Verilog: 4 circuits, main circuit main
module main (
);

  wire clock_1_out, lsb_msb_reg_1_reg, operation_1_load_de_4_lsb_ene__av_r_med_dddd,
       operation_1_load_de_4_msb_ene__av_r_med_dddd, operation_1_load_r_fra_dataminne_gitt_adressen_aaaa,
       operation_1_write_r_til_dataminne_gitt_adressen_aaaa, or_1_out, Reset_out;
  wire [3:0] counter_1_out;
  wire [7:0] lsb_msb_reg_1_output, R_q, ram_1_data;

  Clock clock_1 (.out(clock_1_out));
  Button Reset (.out(Reset_out));
  Counter counter_1 (.Trigger(clock_1_out), .Reset(Reset_out), .Out(counter_1_out));
  RAM #(.addrWidth(4), .bus("asynch")) ram_1 (
    .addr(counter_1_out), .data(ram_1_data), .sel(1'b1), .ld(1'b1), .clr(1'b0));
  Operation operation_1 (
    .in_1(ram_1_data[7:4]), .Load_de_4_LSB_ene__av_R_med_DDDD(operation_1_load_de_4_lsb_ene__av_r_med_dddd),
    .Load_de_4_MSB_ene__av_R_med_DDDD(operation_1_load_de_4_msb_ene__av_r_med_dddd),
    .Load_R_fra_dataminne_gitt_adressen_AAAA(operation_1_load_r_fra_dataminne_gitt_adressen_aaaa),
    .Write_R_til_dataminne_gitt_adressen_AAAA(operation_1_write_r_til_dataminne_gitt_adressen_aaaa));
  LSB___MSB__Reg lsb_msb_reg_1 (
    .in_1(R_q), .in_2(ram_1_data[3:0]),
    .Load_de_4_LSB_ene__av_R_med_DDDD(operation_1_load_de_4_lsb_ene__av_r_med_dddd),
    .Load_de_4_MSB_ene__av_R_med_DDDD(operation_1_load_de_4_msb_ene__av_r_med_dddd),
    .Load_R_fra_dataminne_gitt_adressen_AAAA(operation_1_load_r_fra_dataminne_gitt_adressen_aaaa),
    .Output(lsb_msb_reg_1_output), .Reg(lsb_msb_reg_1_reg));
  or or_1 (or_1_out, operation_1_write_r_til_dataminne_gitt_adressen_aaaa, operation_1_load_r_fra_dataminne_gitt_adressen_aaaa);
  RAM #(.addrWidth(4)) ram_2 (
    .addr(ram_1_data[3:0]), .data(lsb_msb_reg_1_output), .sel(or_1_out), .clk(clock_1_out),
    .ld(operation_1_load_r_fra_dataminne_gitt_adressen_aaaa), .clr(Reset_out));
  Register #(.trigger("falling")) R (
    .D(lsb_msb_reg_1_output), .en(lsb_msb_reg_1_reg), .Q(R_q), .clk(clock_1_out), .clr(Reset_out));
  assign lsb_msb_reg_1_output = operation_1_write_r_til_dataminne_gitt_adressen_aaaa ? R_q : 8'bz;  // Controlled_Buffer controlled_buffer_1

  // Notes on the sheet:
  //   RAM - Programminnet, read only
  //   Data
  //   Address
  //   RAM - Minne
endmodule

module Counter (
  input  Trigger,
  input  Reset,
  output [3:0] Out
);

  wire adder_1_cout, not_1_out;
  wire [3:0] adder_1_out;

  Register #(.width(4), .trigger("falling")) register_1 (
    .D(adder_1_out), .en(not_1_out), .Q(Out), .clk(Trigger), .clr(Reset));
  Adder #(.width(4)) adder_1 (.a(Out), .b(4'b0001), .out(adder_1_out), .cout(adder_1_cout));  // open: cin
  not not_1 (not_1_out, adder_1_cout);
endmodule

module Operation (
  input  [3:0] in_1,
  output Load_de_4_LSB_ene__av_R_med_DDDD,
  output Load_de_4_MSB_ene__av_R_med_DDDD,
  output Load_R_fra_dataminne_gitt_adressen_AAAA,
  output Write_R_til_dataminne_gitt_adressen_AAAA
);

  Decoder #(.select(4), .enable("false")) decoder_1 (
    .out8(Load_de_4_LSB_ene__av_R_med_DDDD), .out9(Load_de_4_MSB_ene__av_R_med_DDDD),
    .out10(Load_R_fra_dataminne_gitt_adressen_AAAA), .out11(Write_R_til_dataminne_gitt_adressen_AAAA),
    .sel(in_1));  // open: out0, out1, out2, out3, out4, out5, out6, out7, out12, out13, out14, out15
endmodule

// SB (R)
module LSB___MSB__Reg (
  input  [7:0] in_1,
  input  [3:0] in_2,
  input  Load_de_4_LSB_ene__av_R_med_DDDD,
  input  Load_de_4_MSB_ene__av_R_med_DDDD,
  input  Load_R_fra_dataminne_gitt_adressen_AAAA,
  output [7:0] Output,
  output Reg
);

  wire not_1_out, or_1_out;
  wire [3:0] controlled_buffer_1_out, controlled_buffer_2_out;

  assign controlled_buffer_1_out = not_1_out ? in_1[3:0] : 4'bz;  // Controlled_Buffer controlled_buffer_1
  not not_1 (not_1_out, Load_de_4_LSB_ene__av_R_med_DDDD);
  assign controlled_buffer_2_out = Load_de_4_LSB_ene__av_R_med_DDDD ? in_1[7:4] : 4'bz;  // Controlled_Buffer controlled_buffer_2
  assign controlled_buffer_1_out = Load_de_4_LSB_ene__av_R_med_DDDD ? in_2 : 4'bz;  // Controlled_Buffer controlled_buffer_3
  assign controlled_buffer_2_out = not_1_out ? in_2 : 4'bz;  // Controlled_Buffer controlled_buffer_4
  or or_1 (or_1_out, Load_de_4_LSB_ene__av_R_med_DDDD, Load_de_4_MSB_ene__av_R_med_DDDD);
  assign Output = or_1_out ? {controlled_buffer_2_out, controlled_buffer_1_out} : 8'bz;  // Controlled_Buffer controlled_buffer_5
  or or_2 (Reg, or_1_out, Load_R_fra_dataminne_gitt_adressen_AAAA);
endmodule
