// Logisim project Half adder.circ as structural Verilog: 1 circuit, main circuit main
module main (
  input  A,
  input  B,
  output Sum,
  output C_out
);

  xor xor_1 (Sum, A, B);
  and and_1 (C_out, A, B);
endmodule
